# Fritzing sketch Untitled Sketch (saved by Fritzing 0.9.3b)
circuit board: 8.46667cm x 5.64444cm
perfboards: 1

parts:
  U1 = attiny85 [package=dip]
  R1 = Resistor [tolerance=±5% resistance=10k package=THT]
  R3 = Resistor [tolerance=±5% resistance=10k package=THT]
  R4 = Resistor [tolerance=±5% resistance=10k package=THT]
  Part2 = BME280 Breakout
  Part1 = NRF24L01+ Breakout Board
  R5 = Resistor [tolerance=±5% resistance=10k package=THT]
  J1 = male pin header, 6 pins [form="♂ (male)"]
  C1 = Ceramic Capacitor [capacitance=0.1µF voltage=6.3V package="100 mil [THT, multilayer]"]
  C3 = Ceramic Capacitor [capacitance=0.1µF voltage=6.3V package="100 mil [THT, multilayer]"]
  VCC1 = Battery
  C2 = Ceramic Capacitor [capacitance=0.1µF voltage=6.3V package="200 mil [THT, multilayer]"]

nets:
  RST: U1.Pin_1, R3.Pin_1, J1.pin5
  CS_BME: U1.Pin_2, R1.Pin_1, Part2.!CS
  CS_NRF: U1.Pin_3, R4.Pin_1, Part1.CS
  GND: U1.Pin_4, Part2.GND, Part1.GND, J1.pin6, C1.0, C3.0, VCC1.-, C2.0
  MOSI: U1.Pin_5, Part2.SDI/SDA, Part1.MOSI, J1.pin4
  MISO: U1.Pin_6, Part2.SDO/ADR, Part1.MISO, R5.Pin_1, J1.pin1
  SCK: U1.Pin_7, Part2.SCK/SCL, Part1.SCK, J1.pin3
  3.3V: U1.Pin_8, R1.Pin_0, R3.Pin_0, R4.Pin_0, Part2.3.3V, Part1.VCC, Part1.CE, R5.Pin_0, C1.1, C3.1, VCC1.+, C2.1
